# Fritzing sketch TTP223_Breakout (saved by Fritzing 0.9.3b)
circuit board: 1cm x 1.3cm
breadboards: 1

parts:
  V-_V+_D0 = female pin header, 3 pins [form="♀ (female)"]
  B = Solder Jumper [package=sj_2s-notrace]
  A = Solder Jumper [package=sj_2s-notrace]
  C1 = Ceramic Capacitor [capacitance="100 nF" package="0603 [SMD, multilayer]"]
  C2 = Ceramic Capacitor [capacitance="100 nF" package="0603 [SMD, multilayer]"]
  R1 = Resistor [tolerance=±5% resistance=220 package="0603 [SMD]"]
  LED1 = LEDs [package=led-0603]
  TTP223 = TTP223 [package=sot23-6]

nets:
  N1: V-_V+_D0.pin1, LED1.A, TTP223.Q
  N2: V-_V+_D0.pin2, B.1, A.2, C1.1, R1.Pin_1, TTP223.Vdd
  N3: V-_V+_D0.pin3, C1.0, C2.1, TTP223.Vss
  N4: B.2, TTP223.TOG
  N5: A.1, TTP223.AHLB
  N6: C2.0, TTP223.I
  N7: R1.Pin_0, LED1.C

notes:
  Touch
  V- V+ DO

custom parts:
  TTP223: Touch Sensor
